# Fritzing sketch Batter Checker PCB (saved by Fritzing 0.9.3b)
circuit board: 3.62336cm x 3.16257cm
breadboards: 1

parts:
  10k = Resistor [tolerance=±5% resistance=10k package=THT]
  100k = Resistor [tolerance=±5% resistance=10k package=THT]
  I/O = Toggle Switch [package=THT]
  -_+ = Screw terminal - 2 pins [package=THT]
  -_+_A_L = female pin header, 4 pins [form="♀ (female)"]
  5_G_L_G_E_V_B_U = female pin header, 8 pins [form="♀ (female)"]
  SEL = Pushbutton [package="[THT]"]
  DWN = Pushbutton [package="[THT]"]
  UP = Pushbutton [package="[THT]"]
  Pro_Micro = Arduino Pro Mini v13

nets:
  N1: 10k.Pin_0, -_+.pin1, SEL.Pin_3, DWN.Pin_3, DWN.Pin_4, UP.Pin_3, UP.Pin_4, Pro_Micro.GND
  N2: 10k.Pin_1, 100k.Pin_1, Pro_Micro.A0
  N3: 100k.Pin_0, -_+.pin2
  N4: I/O.COM, Pro_Micro.RAW
  N5: I/O.L2, 5_G_L_G_E_V_B_U.pin8
  N6: -_+_A_L.pin1, 5_G_L_G_E_V_B_U.pin7, Pro_Micro.RESET
  N7: -_+_A_L.pin2, Pro_Micro.VCC
  N8: -_+_A_L.pin3, Pro_Micro.D2
  N9: -_+_A_L.pin4, Pro_Micro.D3_PWM
  N10: 5_G_L_G_E_V_B_U.pin6, Pro_Micro.A1
  N11: SEL.Pin_1, SEL.Pin_2, Pro_Micro.D6_PWM
  N12: DWN.Pin_1, Pro_Micro.D5_PWM
  N13: UP.Pin_1, Pro_Micro.D4

notes:
  HackBerry Lab
  Battery Meter
