# Fritzing sketch Battery Checker (saved by Fritzing 0.9.3b)
breadboards: 1

parts:
  Pro_Micro2 = Pro Micro
  Charger = PowerBoost 500 Charger
  Squix2 = OLED 0.96" 128x64 I2C SSD1306
  3_7v_LIPO = LIPO-1000mAh [package=lipo-1000]
  B2 = Pushbutton [package="[THT]"]
  B1 = Pushbutton [package="[THT]"]
  B3 = Pushbutton [package="[THT]"]
  Power_Switch = Toggle Switch [package=THT]
  Jumper = Camdenboss CTB0158-2 [part_number=CTB0158-2 package=THT]
  R1 = Resistor [tolerance=±5% resistance=10k package=THT]
  R2 = Resistor [tolerance=±5% resistance=100k package=THT]

nets:
  N1: Pro_Micro2.D2, Squix2.SCA
  N2: Pro_Micro2.D3, Squix2.SCL
  N3: Pro_Micro2.D4, B1.Pin_3, B1.Pin_4
  N4: Pro_Micro2.D5, B2.Pin_3, B2.Pin_4
  N5: Pro_Micro2.D6, B3.Pin_3, B3.Pin_4
  N6: Pro_Micro2.D18/A0, R1.Pin_1, R2.Pin_1
  N7: Pro_Micro2.D19/A1, Charger.LBO
  VCC: Pro_Micro2.VCC, Squix2.VCC
  GND: Pro_Micro2.GND, Charger.GND, Squix2.GND, B2.Pin_1, B2.Pin_2, B1.Pin_1, B1.Pin_2, B3.Pin_1, B3.Pin_2, Jumper.pin1, R1.Pin_0
  N8: Pro_Micro2.RAW, Power_Switch.L1
  N9: Charger.GND_BAT_IN, 3_7v_LIPO.-
  N10: Charger.VBAT_IN, 3_7v_LIPO.+
  N11: Charger.VBAT_OUT, Power_Switch.COM
  N12: Jumper.pin2, R2.Pin_0

custom parts:
  Pro Micro: The SparkFun Pro Micro is a complete USB-based microcontoller development system, in a very small footprint, capable of implementing many types of projects. All programming can be done via the USB port.
